# Fritzing sketch BYOWeatherHAT (saved by Fritzing 0.9.3b)
breadboards: 1

parts:
  J1 = RJ11 Jack [package=rj11-6]
  J2 = RJ11 Jack [package=rj11-6]
  J3 = Camdenboss CTB0158-3 [part_number=CTB0158-3 package=THT]
  J5 = double row female pin header, 40 pins [form="♀ (female)"]
  R1 = Resistor [tolerance=±5% resistance=220 package=THT]
  IC1 = IC, DIP package, 16 pins [chip_label=IC]
  Part1 = RPi hat - blank [part_number=RPI-blank]
  J6 = male pin header, 6 pins [form="♂ (male)"]
  R2 = Resistor [tolerance=±5% resistance=220 package=THT]

nets:
  N1: J1.4, Part1.GPIO6
  N2: J2.2, R1.Pin_1, IC1.pin1
  N3: J2.3, Part1.GND#9, Part1.TXD
  N4: J2.4, J2.5, J3.pin2, IC1.pin9, IC1.pin14, Part1.GND#56
  N5: J3.pin1, J5.pin1, R1.Pin_0, IC1.pin15, IC1.pin16, R2.Pin_0
  N6: J3.pin3, Part1.3.3V, Part1.GPIO4, R2.Pin_1
  N7: J5.pin10, IC1.pin11
  N8: J5.pin11, IC1.pin12
  N9: J5.pin12, IC1.pin13
  N10: IC1.pin3, J6.pin1
  N11: IC1.pin4, J6.pin2
  N12: IC1.pin5, J6.pin3
  N13: IC1.pin6, J6.pin4
  N14: IC1.pin7, J6.pin5
  N15: IC1.pin8, J6.pin6
  N16: IC1.pin10, Part1.SPI_CE0
