# Fritzing sketch ada_2 (saved by Fritzing 0.9.3b)

parts:
  Part7 = Adafruit Perma-Proto HAT [part_number="Adafruit #2314 and #2310"]
  J15 = double row male pin header, 2 pins [form="♂ (male)"]
  J16 = double row male pin header, 2 pins [form="♂ (male)"]
  Part8 = Adafruit BME280

nets:
  N1: Part7.SDA, J15.pin1, Part8.SDI/SDA
  N2: Part7.SCL, J15.pin2, Part8.SCK/SCL
  3.3V: Part7.3.3V, J16.pin2, Part8.VIN
  GND: Part7.GND, J16.pin1, Part8.GND

custom parts:
  Adafruit Perma-Proto HAT: To kick off the Adafruit HAT party, we have this Perma-Proto inspired plug in daughter board. It has a grid of 0.1" prototyping soldering holes for attaching chips, resistors, LED, potentiometers and more. The holes are connected underneath with traces to mimic the solderless breadboards you're familiar. There's also long power strips for +3V, +5V and Ground connections to the Pi. Near the top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
  Adafruit BME280: Bosch has stepped up their game with their new BME280 sensor, an environmental sensor with temperature, barometric pressure and humidity! This sensor is great for all sorts of weather/environmental sensing and can even be used in both I2C and SPI! This precision sensor from Bosch is the best low-cost sensing solution for measuring humidity with ±3% accuracy, barometric pressure with ±1 hPa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
