# Fritzing sketch dht22 (saved by Fritzing 0.9.3b)
breadboards: 1

parts:
  Raspberry_Pi_1 = Raspberry Pi 3 [part_number=RPI-3-V1.2]
  DHT1 = DHT22 Humidity and Temperature Sensor
  R1 = Resistor [tolerance=±5% resistance=4.7k package="0603 [SMD]"]

nets:
  3V3: Raspberry_Pi_1.3v3, DHT1.VDD, R1.Pin_0
  N1: Raspberry_Pi_1.GIPO21, DHT1.GND
  N2: Raspberry_Pi_1.GND, DHT1.DATA, R1.Pin_1
