# Fritzing sketch ds18b20 (saved by Fritzing 0.9.3b)
breadboards: 1

parts:
  Raspberry_Pi_1 = Raspberry Pi 3 [part_number=RPI-3-V1.2]
  J1 = Camdenboss CTB0158-2 [part_number=CTB0158-2 package=THT]
  J2 = Camdenboss CTB0158-2 [part_number=CTB0158-2 package=THT]
  R1 = Resistor [tolerance=±5% resistance=4.7k package="0402 [SMD]"]

nets:
  N1: Raspberry_Pi_1.3v3, J1.terminal_1
  N2: Raspberry_Pi_1.GIPO4, J2.terminal_1
  N3: Raspberry_Pi_1.GND, J1.terminal_2
  N4: J1.pin1, R1.Pin_0
  N5: J2.pin1, R1.Pin_1

notes:
  Wires from DS18B20
