# Fritzing sketch final_circuit (saved by Fritzing 0.9.3b)
breadboards: 1

parts:
  Raspberry_Pi_1 = Raspberry Pi 3 [part_number=RPI-3-V1.2]
  Part2 = Adafruit BME280
  J3 = Camdenboss CTB0158-2 [part_number=CTB0158-2 package=THT]
  J4 = Camdenboss CTB0158-2 [part_number=CTB0158-2 package=THT]
  R2 = Resistor [tolerance=±5% resistance=4.7k package="0402 [SMD]"]
  IC2 = MCP3008 8-channel 10-bit ADC [part_number=MCP3008]
  R3 = Resistor [tolerance=±5% resistance=4.7k package="0402 [SMD]"]
  J5 = RJ11 Jack [package=rj11-6]
  J6 = RJ11 Jack [package=rj11-6]

nets:
  3V3: Raspberry_Pi_1.3v3, Raspberry_Pi_1.3V3, Part2.VIN, J3.pin1, R2.Pin_0, IC2.no_name_yet#15, IC2.no_name_yet#16, J5.5
  N1: Raspberry_Pi_1.GPIO2, Part2.SDO/ADR
  N2: Raspberry_Pi_1.GPIO3, Part2.SCK/SCL
  N3: Raspberry_Pi_1.GIPO4, J4.pin1, R2.Pin_1
  GND: Raspberry_Pi_1.GND, Part2.GND, J3.pin2, IC2.no_name_yet#9, IC2.no_name_yet#14, R3.Pin_0, J5.4, J6.5
  N4: Raspberry_Pi_1.GIPO10, IC2.no_name_yet#11
  N5: Raspberry_Pi_1.GIPO9, IC2.no_name_yet#12
  N6: Raspberry_Pi_1.GIPO11, IC2.no_name_yet#13
  N7: Raspberry_Pi_1.GIPO5, J5.3
  N8: Raspberry_Pi_1.GIPO6, J6.2
  N9: Raspberry_Pi_1.GIPO8, IC2.no_name_yet#10
  N10: IC2.no_name_yet#1, R3.Pin_1, J5.2

notes:
  Wires from DS18B20
  Wind Sensors
  Rain gauge

custom parts:
  Adafruit BME280: Bosch has stepped up their game with their new BME280 sensor, an environmental sensor with temperature, barometric pressure and humidity! This sensor is great for all sorts of weather/environmental sensing and can even be used in both I2C and SPI! This precision sensor from Bosch is the best low-cost sensing solution for measuring humidity with ±3% accuracy, barometric pressure with ±1 hPa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
