# Fritzing sketch final_circuit_strip-stages (saved by Fritzing 0.9.3b)

parts:
  IC5 = MCP3008 8-channel 10-bit ADC [part_number=MCP3008]
  R7 = Resistor [tolerance=±5% resistance=4.7k package="0402 [SMD]"]
  J15 = double row male pin header, 2 pins [form="♂ (male)"]
  J16 = double row male pin header, 2 pins [form="♂ (male)"]
  Part7 = Adafruit Perma-Proto HAT [part_number="Adafruit #2314 and #2310"]
  J19 = double row female pin header, 6 pins [form="♀ (female)"]
  J18 = double row female pin header, 6 pins [form="♀ (female)"]
  R8 = Resistor [tolerance=±5% resistance=4.7k package="0402 [SMD]"]
  J14 = double row female pin header, 6 pins [form="♀ (female)"]

nets:
  N1: IC5.no_name_yet#1, Part7.N$1#160
  N2: IC5.no_name_yet#2, Part7.N$2
  N3: IC5.no_name_yet#3, Part7.N$3
  N4: IC5.no_name_yet#4, Part7.N$4
  N5: IC5.no_name_yet#5, Part7.N$5
  N6: IC5.no_name_yet#6, Part7.N$6
  N7: IC5.no_name_yet#7, Part7.N$8
  N8: IC5.no_name_yet#8, Part7.N$7
  N9: IC5.no_name_yet#9, Part7.N$55#344
  N10: IC5.no_name_yet#10, Part7.N$56#350
  N11: IC5.no_name_yet#11, Part7.N$57#355
  N12: IC5.no_name_yet#12, Part7.N$58#360
  N13: IC5.no_name_yet#13, Part7.N$60#370
  N14: IC5.no_name_yet#14, Part7.N$59#365
  N15: IC5.no_name_yet#15, Part7.N$61#375
  N16: IC5.no_name_yet#16, Part7.N$62#380
  N17: R7.Pin_0, Part7.N$15#229
  N18: R7.Pin_1, Part7.N$11#209
  N19: J15.pin1, Part7.SDA
  N20: J15.pin2, Part7.SCL
  N21: J16.pin1, Part7.GND, Part7.N$12#211, Part7.N$14#221, Part7.N$42#276, Part7.N$55#341, Part7.N$59#361, R8.Pin_0
  N22: J16.pin2, Part7.3.3V, Part7.N$11#208, Part7.N$44#286, Part7.N$61#371, Part7.N$62#376
  N23: Part7.GPIO4, Part7.N$15#230
  N24: Part7.SPI_MOSI, Part7.N$57#351
  N25: Part7.SPI_MISO, Part7.N$58#356
  N26: Part7.SPI_SCLK, Part7.N$60#366
  N27: Part7.SPI_CE0, Part7.N$56#346
  N28: Part7.GPIO5, Part7.N$43#281
  N29: Part7.GPIO6, Part7.N$13#220
  N30: Part7.N$1#159, Part7.N$47#305
  N31: Part7.N$10, J19.pin1, J18.pin1
  N32: Part7.N$11#207, J19.pin2, J18.pin2
  N33: Part7.N$12#212, J19.pin3, J18.pin3
  N34: Part7.N$13#217, J19.pin4, J18.pin4
  N35: Part7.N$14#222, J19.pin5, J18.pin5
  N36: Part7.N$15#227, J19.pin6, J18.pin6
  N37: Part7.N$39, J14.pin6
  N38: Part7.N$41#273, J14.pin5
  N39: Part7.N$41#274, Part7.N$47#304, R8.Pin_1
  N40: Part7.N$42#278, J14.pin4
  N41: Part7.N$43#283, J14.pin3
  N42: Part7.N$44#288, J14.pin2
  N43: Part7.N$45, J14.pin1

custom parts:
  Adafruit Perma-Proto HAT: To kick off the Adafruit HAT party, we have this Perma-Proto inspired plug in daughter board. It has a grid of 0.1" prototyping soldering holes for attaching chips, resistors, LED, potentiometers and more. The holes are connected underneath with traces to mimic the solderless breadboards you're familiar. There's also long power strips for +3V, +5V and Ground connections to the Pi. Near the top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
