# Fritzing sketch final_circuit_strip (saved by Fritzing 0.9.3b)
breadboards: 1

parts:
  Raspberry_Pi_1 = Raspberry Pi 3 [part_number=RPI-3-V1.2]
  Part2 = Adafruit BME280
  J3 = Camdenboss CTB0158-2 [part_number=CTB0158-2 package=THT]
  J4 = Camdenboss CTB0158-2 [part_number=CTB0158-2 package=THT]  # not connected
  R2 = Resistor [tolerance=±5% resistance=4.7k package="0402 [SMD]"]
  IC2 = MCP3008 8-channel 10-bit ADC [part_number=MCP3008]
  R3 = Resistor [tolerance=±5% resistance=4.7k package="0402 [SMD]"]
  J5 = RJ11 Jack [package=rj11-6]
  J6 = RJ11 Jack [package=rj11-6]
  Part5 = Adafruit BME280  # not connected
  IC4 = MCP3008 8-channel 10-bit ADC [part_number=MCP3008]
  J13 = double row female pin header, 6 pins [form="♀ (female)"]
  J14 = double row female pin header, 6 pins [form="♀ (female)"]
  J15 = Camdenboss CTB0158-2 [part_number=CTB0158-2 package=THT]
  J16 = Camdenboss CTB0158-2 [part_number=CTB0158-2 package=THT]
  Part4 = Adafruit Perma-Proto HAT [part_number="Adafruit #2314 and #2310"]
  R5 = Resistor [tolerance=±5% resistance=4.7k package="0402 [SMD]"]
  R6 = Resistor [tolerance=±5% resistance=4.7k package="0402 [SMD]"]
  Part6 = Adafruit BME280

nets:
  N1: Raspberry_Pi_1.GPIO2, Part2.SDO/ADR
  N2: Raspberry_Pi_1.GPIO3, Part2.SCK/SCL
  N3: Raspberry_Pi_1.GIPO4, R2.Pin_1
  GND: Raspberry_Pi_1.GND, Part2.GND, J6.4
  3V3: Raspberry_Pi_1.3V3, Part2.VIN
  N4: Raspberry_Pi_1.GIPO10, IC2.no_name_yet#11
  N5: Raspberry_Pi_1.GIPO9, IC2.no_name_yet#12
  N6: Raspberry_Pi_1.GIPO11, IC2.no_name_yet#13
  N7: Raspberry_Pi_1.GIPO5, J5.3
  N8: Raspberry_Pi_1.GIPO6, J6.3
  N9: Raspberry_Pi_1.GIPO8, IC2.no_name_yet#10
  N10: J3.pin1, R2.Pin_0, IC2.no_name_yet#15, IC2.no_name_yet#16, J5.5
  N11: J3.pin2, IC2.no_name_yet#9, IC2.no_name_yet#14, R3.Pin_0, J5.4
  N12: IC2.no_name_yet#1, R3.Pin_1, J5.2
  N13: IC4.no_name_yet#1, Part4.N$1#160
  N14: IC4.no_name_yet#2, Part4.N$2
  N15: IC4.no_name_yet#3, Part4.N$3
  N16: IC4.no_name_yet#4, Part4.N$4
  N17: IC4.no_name_yet#5, Part4.N$5
  N18: IC4.no_name_yet#6, Part4.N$6
  N19: IC4.no_name_yet#7, Part4.N$8
  N20: IC4.no_name_yet#8, Part4.N$7
  N21: IC4.no_name_yet#9, Part4.N$55#344
  N22: IC4.no_name_yet#10, Part4.N$56#350
  N23: IC4.no_name_yet#11, Part4.N$57#355
  N24: IC4.no_name_yet#12, Part4.N$58#360
  N25: IC4.no_name_yet#13, Part4.N$60#370
  N26: IC4.no_name_yet#14, Part4.N$59#365
  N27: IC4.no_name_yet#15, Part4.N$61#375
  N28: IC4.no_name_yet#16, Part4.N$62#380
  N29: J13.pin1, Part4.N$10
  N30: J13.pin2, Part4.N$11
  N31: J13.pin3, Part4.N$12#212
  N32: J13.pin4, Part4.N$13#217
  N33: J13.pin5, Part4.N$14
  N34: J13.pin6, Part4.N$15
  N35: J14.pin1, Part4.N$45
  N36: J14.pin2, Part4.N$44#287
  N37: J14.pin3, Part4.N$43#282
  N38: J14.pin4, Part4.N$42#277
  N39: J14.pin5, Part4.N$41#272
  N40: J14.pin6, Part4.N$39
  N41: J15.pin1, Part4.N$18#239
  N42: J15.pin2, Part4.N$19#244
  N43: J16.pin1, Part4.N$22#259
  N44: J16.pin2, Part4.N$23
  N45: Part4.SDA, Part6.SDO/ADR
  N46: Part4.SCL, Part6.SCK/SCL
  N47: Part4.GPIO4, Part4.N$18#237
  N48: Part4.SPI_MOSI, Part4.N$57#351
  N49: Part4.SPI_MISO, Part4.N$58#356
  N50: Part4.SPI_SCLK, Part4.N$60#366
  N51: Part4.SPI_CE0, Part4.N$56#346
  N52: Part4.GPIO5, Part4.N$42#276
  N53: Part4.GPIO6, Part4.N$12#215
  3.3V: Part4.3.3V, Part4.N$22#256, Part4.N$44#286, Part4.N$61#371, Part4.N$62#376, R5.Pin_1, Part6.3.3V
  GND_2: Part4.GND, Part4.N$13#216, Part4.N$19#241, Part4.N$43#281, Part4.N$55#341, Part4.N$59#361, Part6.GND
  N54: Part4.N$1#159, Part4.N$47#305
  N55: Part4.N$18#238, R6.Pin_1
  N56: Part4.N$22#258, R6.Pin_0
  N57: Part4.N$41#274, Part4.N$47#304
  N58: Part4.N$47#303, R5.Pin_0

notes:
  Wind Sensors
  Rain gauge

custom parts:
  Adafruit BME280: Bosch has stepped up their game with their new BME280 sensor, an environmental sensor with temperature, barometric pressure and humidity! This sensor is great for all sorts of weather/environmental sensing and can even be used in both I2C and SPI! This precision sensor from Bosch is the best low-cost sensing solution for measuring humidity with ±3% accuracy, barometric pressure with ±1 hPa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
  Adafruit Perma-Proto HAT: To kick off the Adafruit HAT party, we have this Perma-Proto inspired plug in daughter board. It has a grid of 0.1" prototyping soldering holes for attaching chips, resistors, LED, potentiometers and more. The holes are connected underneath with traces to mimic the solderless breadboards you're familiar. There's also long power strips for +3V, +5V and Ground connections to the Pi. Near the top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
